// Logisim project Pipeline.circ as structural Verilog: 4 circuits, main circuit main
module main (
  input  [15:0] FL,
  input  [15:0] FH,
  input  [3:0] Symbol,
  input  [4:0] nsyms,
  input  Bool_Flag,
  output [15:0] RANGE,
  output [23:0] LOW
);

  wire register_6_q, register_7_q, register_8_q, stage_1_1_bool_flag_2, stage_1_1_comp_mux_1,
       stage_2_1_comp_mux_1_2;
  wire [1:0] register_9_q, stage_2_1_bool_symbol;
  wire [3:0] register_3_q, stage_1_1_symbol_2;
  wire [4:0] register_10_q, register_15_q, stage_2_1_d, stage_3_1_cnt_2;
  wire [15:0] register_1_q, register_2_q, register_4_q, register_5_q, register_11_q, register_12_q,
       register_13_q, register_14_q, stage_1_1_lut_u, stage_1_1_lut_v, stage_1_1_uu, stage_1_1_vv,
       stage_2_1_initial_range, stage_2_1_range_ready, stage_2_1_u, stage_2_1_v_bool, stage_3_1_range;
  wire [23:0] stage_3_1_low_2;

  stage_1 stage_1_1 (
    .FL(FL), .FH(FH), .Symbol(Symbol), .Number_of_symbols__nsyms(nsyms), .Bool_Flag(Bool_Flag),
    .LUT_U(stage_1_1_lut_u), .LUT_V(stage_1_1_lut_v), .Symbol_2(stage_1_1_symbol_2), .UU(stage_1_1_uu),
    .VV(stage_1_1_vv), .COMP_Mux_1(stage_1_1_comp_mux_1), .Bool_Flag_2(stage_1_1_bool_flag_2));
  Register #(.width(16)) register_1 (.D(stage_1_1_lut_u), .Q(register_1_q));  // open: en, clk, clr
  Register #(.width(16)) register_2 (.D(stage_1_1_lut_v), .Q(register_2_q));  // open: en, clk, clr
  Register #(.width(4)) register_3 (.D(stage_1_1_symbol_2), .Q(register_3_q));  // open: en, clk, clr
  Register #(.width(16)) register_4 (.D(stage_1_1_uu), .Q(register_4_q));  // open: en, clk, clr
  Register #(.width(16)) register_5 (.D(stage_1_1_vv), .Q(register_5_q));  // open: en, clk, clr
  Register #(.width(1)) register_6 (.D(stage_1_1_comp_mux_1), .Q(register_6_q));  // open: en, clk, clr
  Register #(.width(1)) register_7 (.D(stage_1_1_bool_flag_2), .Q(register_7_q));  // open: en, clk, clr
  stage_2 stage_2_1 (
    .LUT_U(register_1_q), .LUT_V(register_2_q), .Symbol(register_3_q), .UU(register_4_q), .VV(register_5_q),
    .Comp_Mux_1(register_6_q), .Bool_Flag(register_7_q), .Range(register_14_q),
    .Comp_Mux_1_2(stage_2_1_comp_mux_1_2), .Bool_Symbol(stage_2_1_bool_symbol), .D(stage_2_1_d),
    .U(stage_2_1_u), .V_Bool(stage_2_1_v_bool), .Initial_Range(stage_2_1_initial_range),
    .Range_Ready(stage_2_1_range_ready));
  Register #(.width(1)) register_8 (.D(stage_2_1_comp_mux_1_2), .Q(register_8_q));  // open: en, clk, clr
  Register #(.width(2)) register_9 (.D(stage_2_1_bool_symbol), .Q(register_9_q));  // open: en, clk, clr
  Register #(.width(5)) register_10 (.D(stage_2_1_d), .Q(register_10_q));  // open: en, clk, clr
  Register #(.width(16)) register_11 (.D(stage_2_1_u), .Q(register_11_q));  // open: en, clk, clr
  Register #(.width(16)) register_12 (.D(stage_2_1_v_bool), .Q(register_12_q));  // open: en, clk, clr
  Register #(.width(16)) register_13 (.D(stage_2_1_initial_range), .Q(register_13_q));  // open: en, clk, clr
  Register #(.width(16)) register_14 (.D(stage_2_1_range_ready), .Q(register_14_q));  // open: en, clk, clr
  stage_3 stage_3_1 (
    .CNT(register_15_q), .Comp_Mux_1(register_8_q), .Bool_Symbol(register_9_q), .D(register_10_q),
    .U(register_11_q), .V_Bool(register_12_q), .Initial_Range(register_13_q), .Range_Ready(register_14_q),
    .Low(LOW), .CNT_2(stage_3_1_cnt_2), .Range(stage_3_1_range), .Low_2(stage_3_1_low_2));
  Register #(.width(5)) register_15 (.D(stage_3_1_cnt_2), .Q(register_15_q));  // open: en, clk, clr
  Register #(.width(16)) register_16 (.D(stage_3_1_range), .Q(RANGE));  // open: en, clk, clr
  Register #(.width(24)) register_17 (.D(stage_3_1_low_2), .Q(LOW));  // open: en, clk, clr

  // Notes on the sheet:
  //   range ready
  //   counter
  //   Low
endmodule

// Stage 1
module stage_1 (
  input  [15:0] FL,
  input  [15:0] FH,
  input  [3:0] Symbol,
  input  [4:0] Number_of_symbols__nsyms,
  input  Bool_Flag,
  output [15:0] LUT_U,
  output [15:0] LUT_V,
  output [3:0] Symbol_2,
  output [15:0] UU,
  output [15:0] VV,
  output COMP_Mux_1,
  output Bool_Flag_2
);
endmodule

// Stage 2
module stage_2 (
  input  [15:0] LUT_U,
  input  [15:0] LUT_V,
  input  [3:0] Symbol,
  input  [15:0] UU,
  input  [15:0] VV,
  input  Comp_Mux_1,
  input  Bool_Flag,
  input  [15:0] Range,
  output Comp_Mux_1_2,
  output [1:0] Bool_Symbol,
  output [4:0] D,
  output [15:0] U,
  output [15:0] V_Bool,
  output [15:0] Initial_Range,
  output [15:0] Range_Ready
);
endmodule

// Stage 3
module stage_3 (
  input  [4:0] CNT,
  input  Comp_Mux_1,
  input  [1:0] Bool_Symbol,
  input  [4:0] D,
  input  [15:0] U,
  input  [15:0] V_Bool,
  input  [15:0] Initial_Range,
  input  [15:0] Range_Ready,
  input  [23:0] Low,
  output [4:0] CNT_2,
  output [15:0] Range,
  output [23:0] Low_2
);
endmodule
